# Fritzing sketch Ampela (saved by Fritzing 0.9.2b)
circuit board: 10cm x 5cm
breadboards: 1

parts:
  R1 = Resistor [tolerance=±5% resistance=220 package=THT]
  R2 = Resistor [tolerance=±5% resistance=220 package=THT]
  LED_rot = LED - 5mm [color="Red (633nm)" package="5 mm [THT]"]
  LED_gelb = LED - 5mm [color="Yellow (595nm)" package="5 mm [THT]"]
  LED_grün = LED - 5mm [color="Green (565nm)" package="5 mm [THT]"]
  SW1 = DIP SWITCH [package=dipswitch-02]
  R3 = Resistor [tolerance=±5% resistance=220 package=THT]
  Taster_für_Bedarfsanforderung = Pushbutton [package="[THT]"]
  4-POL-DIP-Switch = DIP SWITCH [package=dipswitch-02]
  R4 = Resistor [tolerance=±5% resistance=220 package=THT]
  LED_rot_(Fuß) = LED - 5mm [color="Red (633nm)" package="5 mm [THT]"]
  R5 = Resistor [tolerance=±5% resistance=220 package=THT]
  LED_grün_(Fuß) = LED - 5mm [color="Green (565nm)" package="5 mm [THT]"]
  J1 = female pin header, 4 pins [form="♀ (female)"]
  R6 = Resistor [tolerance=±5% resistance=1.7k package=THT]
  R7 = Resistor [tolerance=±5% resistance=1.7k package=THT]
  Bauteil1 = Arduino Nano (Rev3.0)
  J2 = female pin header, 4 pins [form="♀ (female)"]

nets:
  N1: R1.Pin_0, Bauteil1.D5
  N2: R1.Pin_1, LED_gelb.anode
  N3: R2.Pin_0, Bauteil1.D4
  N4: R2.Pin_1, LED_grün.anode
  N5: LED_rot.cathode, LED_gelb.cathode, LED_grün.cathode, SW1.1, SW1.2, Taster_für_Bedarfsanforderung.Pin_1, Taster_für_Bedarfsanforderung.Pin_2, 4-POL-DIP-Switch.1, 4-POL-DIP-Switch.2, LED_rot_(Fuß).cathode, LED_grün_(Fuß).cathode, J1.pin4, Bauteil1.GND, J2.pin4
  N6: LED_rot.anode, R3.Pin_1
  N7: SW1.3, Bauteil1.D8
  N8: SW1.4, Bauteil1.D7
  N9: R3.Pin_0, Bauteil1.D6
  N10: Taster_für_Bedarfsanforderung.Pin_4, Bauteil1.D11/MOSI
  N11: 4-POL-DIP-Switch.3, Bauteil1.D10
  N12: 4-POL-DIP-Switch.4, Bauteil1.D9
  N13: R4.Pin_0, Bauteil1.D3
  N14: R4.Pin_1, LED_rot_(Fuß).anode
  N15: R5.Pin_0, Bauteil1.D2
  N16: R5.Pin_1, LED_grün_(Fuß).anode
  N17: J1.pin1, R7.Pin_1, Bauteil1.A5, J2.pin1
  N18: J1.pin2, R6.Pin_0, R7.Pin_0, Bauteil1.5V, J2.pin2
  N19: J1.pin3, R6.Pin_1, Bauteil1.A4, J2.pin3

// code stored in the sketch: Ampel.ino
#include <Wire.h>
void setup()
{
  Serial.begin(9600);
  Wire.begin();
}
void loop()
{
  //Eingabe lesen
  byte eingabe = Serial.read();
  if(eingabe != 255)
    Verschicken(eingabe, 4);
}

void Verschicken(byte nachricht, int device)
{
  byte richtig = 0;
  if(nachricht >= 49 && nachricht <= 57)
    richtig = 1;
  if(nachricht >= 65 && nachricht <= 90)
    richtig = 1;
  if(nachricht >= 97 && nachricht <= 122)
  {
    nachricht = nachricht - 32;
    richtig = 1;
  }
  if(richtig == 1)
  {
    Wire.beginTransmission(device);
    Wire.write(nachricht);
    Serial.print(nachricht);
    Serial.println(" wurde gesendet.");
    Wire.endTransmission();
  }
}
